# Fritzing sketch FabolousNeopixelFirmware (saved by Fritzing 0.8.7b)
breadboards: 1

parts:
  Bauteil1 = Arduino Micro (Rev3)
  X1 = USB Connectors [package=usb-microb]
  C1 = Electrolytic Capacitor [capacitance=100nF package="100 mil [THT, electrolytic]"]
  IR1 = TSOP312.., 314.. [package=THT]
  NEOPIXEL1 = Neopixel Strip -- White (30/m)
  R1 = Resistor [tolerance=±5% resistance=470 package=THT]

nets (from the schematic view):
  GND: Bauteil1.GND, X1.GND, C1.-, IR1.GND, NEOPIXEL1.GND
  N1: Bauteil1.D5_PWM, IR1.Data
  N2: Bauteil1.D6_PWM/A7, R1.Pin_0
  VIN: Bauteil1.VIN, X1.VBUS, C1.+, IR1.Vs, NEOPIXEL1.+5V
  N3: NEOPIXEL1.Din, R1.Pin_1

custom parts:
  Neopixel Strip -- White (30/m): These NeoPixel strips have 30 digitally-addressable pixel LEDs per meter and are very affordable and are only 12.5 mm wide, 10 mm if you remove the strip from the casing.
